# Fritzing sketch arduino-nano-motor-controller (saved by Fritzing 1.0.1rc)
circuit board: 4.45408cm x 5.64444cm
breadboards: 1

parts:
  P+_P-_D+_D-_E+_E-_A+_A- = female pin header, 8 pins [form="♀ (female)"]
  nano = Arduino Nano (Rev3.0) (ICSP)
  J1 = female pin header, 8 pins [form="♀ (female)"]
  7805 = Voltage Regulator [package=78xxl]
  R1 = Resistor [tolerance=±5% power=0.25 resistance=100k package=THT]
  R2 = Resistor [tolerance=±5% power=0.25 resistance=100k package=THT]
  R3 = Resistor [tolerance=±5% power=0.25 resistance=100k package=THT]
  C1 = Ceramic Capacitor [capacitance=100nF voltage=35V package="100 mil [THT, multilayer]"]
  C2 = Electrolytic Capacitor [capacitance=1µF voltage=35V package="100 mil [THT, electrolytic]"]
  C3 = Ceramic Capacitor [capacitance=100nF voltage=35V package="100 mil [THT, multilayer]"]
  C4 = Electrolytic Capacitor [capacitance=1µF voltage=35V package="100 mil [THT, electrolytic]"]
  D1 = Rectifier Diode [part_number=1N4001 package="300 mil [THT]"]
  D2 = Rectifier Diode [part_number=1N4001 package="300 mil [THT]"]
  J2 = Screw terminal - 2 pins [package=THT]
  J3 = female pin header, 3 pins [form="♀ (female)"]
  J4 = female pin header, 2 pins [form="♀ (female)"]
  J5 = female pin header, 2 pins [form="♀ (female)"]

nets:
  GND: P+_P-_D+_D-_E+_E-_A+_A-.pin1, P+_P-_D+_D-_E+_E-_A+_A-.pin3, P+_P-_D+_D-_E+_E-_A+_A-.pin5, P+_P-_D+_D-_E+_E-_A+_A-.pin7, nano.GND, J1.pin2, J1.pin4, J1.pin6, J1.pin8, 7805.GND, R1.Pin_0, R2.Pin_0, R3.Pin_0, C1.0, C2.-, C3.0, C4.-, J2.pin1, J3.pin1
  ALM: P+_P-_D+_D-_E+_E-_A+_A-.pin2, nano.D2, J1.pin7
  ENA: P+_P-_D+_D-_E+_E-_A+_A-.pin4, nano.D7, J1.pin5, R3.Pin_1
  DIR: P+_P-_D+_D-_E+_E-_A+_A-.pin6, nano.D8, J1.pin3, R2.Pin_1
  PUL: P+_P-_D+_D-_E+_E-_A+_A-.pin8, nano.D9, J1.pin1, R1.Pin_1
  LED: nano.D5, J3.pin2
  5V: nano.VIN, 7805.OUT, C1.1, C2.+, D1.anode, J4.pin2
  12V: 7805.IN, C3.1, C4.+, D1.cathode, D2.cathode, J5.pin1
  N1: D2.anode, J2.pin2
  N2: J3.pin3, J4.pin1, J5.pin2
