# Fritzing sketch arduino-nano-relays (saved by Fritzing 1.0.1rc)
circuit board: 1.90375cm x 4.45982cm
breadboards: 1

parts:
  Part1 = Arduino Nano (Rev3.0) (ICSP)
  R1 = Resistor [tolerance=±5% power=0.25 resistance=220 package=THT]
  J1 = female pin header, 10 pins [form="♀ (female)"]

nets:
  N1: Part1.D2, J1.pin2
  N2: Part1.D3, J1.pin3
  N3: Part1.D4, J1.pin4
  N4: Part1.D5, J1.pin5
  N5: Part1.D6, J1.pin6
  N6: Part1.D7, J1.pin7
  N7: Part1.D8, J1.pin8
  N8: Part1.D9, J1.pin9
  N9: Part1.GND, J1.pin1
  N10: Part1.RESET, R1.Pin_0
  N11: Part1.5V, R1.Pin_1, J1.pin10
