# Fritzing sketch wiring (saved by Fritzing 1.0.1rc)
breadboards: 1

parts:
  electronics = female pin header, 2 pins [form="♀ (female)"]
  LED = LTE-302 [package=lte-302]
  SP1 = SPEAKER [package=pcb_mount_speaker]
  LED1 = LTE-302 [package=lte-302]  # not connected
  pump = Vibration Motor- ROB-08449 [package=vibe-motor-10mm]
  electronics1 = female pin header, 2 pins [form="♀ (female)"]
  LED2 = LTE-302 [package=lte-302]
  pump1 = Vibration Motor- ROB-08449 [package=vibe-motor-10mm]
  electronics2 = female pin header, 2 pins [form="♀ (female)"]
  LED3 = LTE-302 [package=lte-302]
  pump2 = Vibration Motor- ROB-08449 [package=vibe-motor-10mm]
  LED4 = LTE-302 [package=lte-302]  # not connected
  SP2 = SPEAKER [package=pcb_mount_speaker]
  MIC1 = Microphone
  MIC2 = Microphone
  MIC3 = Microphone
  FAN = Vibration Motor- ROB-08449 [package=vibe-motor-10mm]  # not connected
  MIC4 = Microphone

nets:
  24V/driver 1: electronics.pin1, electronics1.pin1, electronics2.pin1
  12V: LED.A, SP1.+, pump.+, LED2.A, pump1.+, LED3.A, pump2.+, SP2.+, MIC1.pin1, MIC2.pin1, MIC3.pin1, MIC4.pin1

notes:
  DMX
  mixer
